// Logisim project Time.circ as structural Verilog
module main (
);

  wire clock_1_out, clockcore_1_am_pm, controlunit_1_hour, controlunit_1_min, controlunit_1_run,
       controlunit_1_sec, M_out, MS, MS_Test_out, R_out, S_out;
  wire [2:0] controlunit_1_state, stopwatch_1_state;
  wire [3:0] clockcore_1_hours;
  wire [5:0] clockcore_1_minutes, clockcore_1_seconds;

  Button M (.out(M_out));
  Button S (.out(S_out));
  Clock clock_1 (.out(clock_1_out));
  Button button_1 ();  // open: out
  Button R (.out(R_out));
  Button MS_Test (.out(MS_Test_out));
  _7_Segment_Display u_7_segment_display_1 ();  // open: g, f, a, b, e, d, c, dp
  and and_1 (MS, M_out, S_out);
  // Probe on M_out
  Stopwatch stopwatch_1 (.State(stopwatch_1_state));
  ControlUnit controlunit_1 (
    .M(M_out), .S(S_out), .Clk(clock_1_out), .MS_Test(MS_Test_out), .R(R_out), .Hour(controlunit_1_hour),
    .Min(controlunit_1_min), .Sec(controlunit_1_sec), .Run(controlunit_1_run), .State(controlunit_1_state));
  // Probe on stopwatch_1_state
  LED led_1 (.in(controlunit_1_sec));
  LED led_2 (.in(controlunit_1_min));
  LED led_3 (.in(controlunit_1_hour));
  LED led_4 (.in(controlunit_1_run));
  // Probe on controlunit_1_state
  ClockCore clockcore_1 (
    .RESET_TIME(R_out), .CLK_1Hz(clock_1_out), .INC_SEC(controlunit_1_sec), .RUN(controlunit_1_run),
    .INC_HOUR(controlunit_1_hour), .INC_MIN(controlunit_1_min), .SECONDS(clockcore_1_seconds),
    .MINUTES(clockcore_1_minutes), .HOURS(clockcore_1_hours), .AM_PM(clockcore_1_am_pm));  // open: in_7, in_8
  // Probe on clockcore_1_seconds
  // Probe on clockcore_1_minutes
  // Probe on clockcore_1_hours
  // Probe on clockcore_1_am_pm
endmodule

module ClockCore (
  input  RESET_TIME,
  input  CLK_1Hz,
  input  INC_SEC,
  input  RUN,
  input  INC_HOUR,
  input  INC_MIN,
  input  in_7,
  input  in_8,
  output [5:0] SECONDS,
  output [5:0] MINUTES,
  output [3:0] HOURS,
  output AM_PM
);

  wire and_1_out, and_2_out, and_3_out, clock_1_out, counter_1_carry, Minutes_Counter_carry, not_1_out,
       or_1_out, or_2_out, or_3_out, Seconds_Counter_carry;

  and and_1 (and_1_out, CLK_1Hz, INC_SEC);
  or or_1 (or_1_out, and_1_out, RUN);
  Clock clock_1 (.out(clock_1_out));
  Counter #(.max('h3b), .width(6)) Seconds_Counter (
    .clr(RESET_TIME), .count(or_1_out), .clk(clock_1_out), .carry(Seconds_Counter_carry), .Q(SECONDS));  // open: load, up, D
  and and_2 (and_2_out, INC_MIN, RUN);
  Counter #(.max('h3b), .width(6)) Minutes_Counter (
    .clr(RESET_TIME), .count(or_2_out), .clk(Seconds_Counter_carry), .carry(Minutes_Counter_carry),
    .Q(MINUTES));  // open: load, up, D
  or or_2 (or_2_out, and_2_out, in_8);
  and and_3 (and_3_out, INC_HOUR, RUN);
  or or_3 (or_3_out, and_3_out, in_7);
  Counter #(.max('hb), .width(4)) counter_1 (
    .clr(RESET_TIME), .count(or_3_out), .clk(Minutes_Counter_carry), .carry(counter_1_carry), .Q(HOURS));  // open: load, up, D
  not not_1 (not_1_out, AM_PM);
  D_Flip_Flop AM_PM_FlipFlop (.D(not_1_out), .clk(counter_1_carry), .Q(AM_PM), .reset(RESET_TIME));  // open: Qn, preset
endmodule

module AlarmUnit (
);

  Multiplexer multiplexer_1 ();  // open: in0, in1, out, sel
  Register #(.width(4)) register_1 ();  // open: D, en, clk, Q, clr
  Register #(.width(6)) register_2 ();  // open: D, en, clk, Q, clr
endmodule

module Stopwatch (
  output [2:0] State
);


  assign State = 3'b110;
endmodule

module ControlUnit (
  input  M,
  input  S,
  input  Clk,
  input  MS_Test,
  input  R,
  output Hour,
  output Min,
  output Sec,
  output Run,
  output [2:0] State
);

  wire and_1_out, and_2_out, and_3_out, and_9_out, and_10_out, D0, D1, D2, D_of_T0, D_of_T1, D_of_T2,
       next_q0_ms, next_q1_ms, next_q2_ms, nq0, nq1, nq2, s000, s001, s010, s100, TRANS;

  or or_1 (next_q0_ms, s000, s010, s100);
  or or_2 (next_q1_ms, s001, s010);
  and and_1 (and_1_out, s010, MS_Test);
  and and_2 (and_2_out, s100, MS_Test);
  or or_3 (D0, and_1_out, and_2_out);
  Button button_1 ();  // open: out
  Button button_2 ();  // open: out
  Button button_3 ();  // open: out
  and and_3 (and_3_out, M, S);
  and and_4 (s000, nq0, nq1, nq2);
  and and_5 (s010, State[1], nq0, nq2);
  and and_6 (s100, State[2], nq0, nq1);
  and and_7 (s001, State[0], nq1, nq2);
  and and_8 (next_q2_ms, State[0], State[1], nq2);
  and and_9 (and_9_out, s001, MS_Test);
  and and_10 (and_10_out, next_q2_ms, MS_Test);
  D_Flip_Flop T0 (.D(MS_Test), .clk(Clk), .Q(State[0]), .reset(R));  // open: Qn, preset
  D_Flip_Flop T1 (.D(D1), .clk(Clk), .Q(State[1]), .reset(R));  // open: Qn, preset
  D_Flip_Flop T2 (.D(D2), .clk(Clk), .Q(State[2]), .reset(R));  // open: Qn, preset
  or or_4 (D1, and_9_out, and_10_out);
  or or_5 (TRANS, M, S);
  not not_1 (nq0, State[0]);
  not not_2 (nq1, State[1]);
  not not_3 (nq2, State[2]);
  Multiplexer #(.select(2)) multiplexer_1 (
    .in0(State[0]), .in1(next_q0_ms), .in2(1'b0), .in3(1'b0), .out(D_of_T0), .sel({MS_Test, M}));
  Multiplexer #(.select(2)) multiplexer_2 (
    .in0(State[1]), .in1(next_q1_ms), .in2(1'b0), .in3(1'b0), .out(D_of_T1), .sel({MS_Test, M}));
  Multiplexer #(.select(2)) multiplexer_3 (
    .in0(State[2]), .in1(next_q2_ms), .in2(1'b0), .in3(1'b0), .out(D_of_T2), .sel({MS_Test, M}));
  and and_11 (D2, next_q2_ms, MS_Test);
  and INC_HOUR (Hour, S, State[0], nq1, nq2);
  and INC_MIN (Min, nq2, State[1], nq0, S);
  and INC_SEC (Sec, nq2, State[1], State[0], S);
  and INC_RUN (Run, nq0, nq1, State[2], S);

  // Other names for the same wires on the sheet: MS = MS_Test; s011 = next_q2_ms; q0 = State[0]; q1 = State[1];
  //   q2 = State[2]
endmodule
