// Logisim project ddd.circ as structural Verilog: 21 circuits, main circuit main
module main (
  input  R,
  output [3:0] Stat
);

  wire alarm_1_active, alarm_1_alr, AM, AM_PM, AM_PM_AL, AM_PM_TZ, and_1_out, and_2_out, and_3_out, BH, BM,
       BS, buttonconv_1_impuls, buttonconv_1_x1, buttonconv_1_x2, Clk, clock_1_out, clock_2_out, clock_3_out,
       decoder_i1_1_inc_hour, decoder_i1_1_inc_min, decoder_i1_1_inc_sec, demultiplexer_1_out0,
       demultiplexer_1_out1, displaymux_1_b_h, displaymux_1_b_m, displaymux_1_b_s, i1, i2, i3, i4, i5, i6,
       i_H, i_M, L1, L2, L3, L4, L5, L6, L7, L8, LH, LM, LS, M_out, MS_out, or_1_out, or_2_out, or_3_out,
       P_out, S_out, sound_1_match, TZ;
  wire [3:0] A_H, displaymux_1_d_h, Hours, Hours_TZ, splitterhours_1_tens, splitterhours_1_unit,
       splittertime_1_out_2, splittertime_1_out_3, splittertime_2_out_2, splittertime_2_out_3;
  wire [5:0] A_M, displaymux_1_d_m, displaymux_1_d_s, Minutes, Seconds, SW_MIN, SW_SEC;
  wire [6:0] controlled_buffer_1_out, controlled_buffer_2_out, controlled_buffer_3_out,
       controlled_buffer_4_out, controlled_buffer_5_out, controlled_buffer_6_out,
       indicatorconvector_1_output, indicatorconvector_2_output, indicatorconvector_3_output,
       indicatorconvector_4_output, indicatorconvector_5_output, indicatorconvector_6_output;

  Button S (.out(S_out));
  Button M (.out(M_out));
  Button MS (.out(MS_out));
  Button P (.out(P_out));
  Gen gen_1 (.CLk(Clk));
  LED u_AM (.in(demultiplexer_1_out0));
  LED PM (.in(demultiplexer_1_out1));
  Demultiplexer demultiplexer_1 (.out0(demultiplexer_1_out0), .out1(demultiplexer_1_out1), .in(1'b1), .sel(AM));
  IndicatorConvector indicatorconvector_1 (.\input (splitterhours_1_tens), .\output (indicatorconvector_1_output));
  SplitterHours splitterhours_1 (.Hours(displaymux_1_d_h), .Tens(splitterhours_1_tens), .Unit(splitterhours_1_unit));
  ButtonConv buttonconv_1 (
    .S(S_out), .M(M_out), .MS(MS_out), .P(P_out), .X1(buttonconv_1_x1), .X2(buttonconv_1_x2),
    .impuls(buttonconv_1_impuls));
  _7_Segment_Display u_7_segment_display_1 (
    .g(controlled_buffer_1_out[6]), .f(controlled_buffer_1_out[5]), .a(controlled_buffer_1_out[4]),
    .b(controlled_buffer_1_out[3]), .e(controlled_buffer_1_out[0]), .d(controlled_buffer_1_out[1]),
    .c(controlled_buffer_1_out[2]));  // open: dp
  assign controlled_buffer_1_out = and_1_out ? indicatorconvector_1_output : 7'bz;  // Controlled_Buffer controlled_buffer_1
  and and_1 (and_1_out, L1, or_1_out, LH);
  or or_1 (or_1_out, clock_1_out, BH);
  Clock #(.highDuration(2)) clock_1 (.out(clock_1_out));
  DisplayMux displaymux_1 (
    .State(Stat), .H(Hours), .TZ_H(Hours_TZ), .L4(L4), .A_H(A_H), .L5(L5), .M(Minutes), .SW_M(SW_MIN),
    .A_M(A_M), .S(Seconds), .SW_SEC(SW_SEC), .L6(L6), .L7(L7), .L8(L8), .AM_PM(AM_PM), .AM_PM_AL(AM_PM_AL),
    .AM_PM_TZ(AM_PM_TZ), .D_H(displaymux_1_d_h), .D_M(displaymux_1_d_m), .D_S(displaymux_1_d_s), .L_H(LH),
    .L_M(LM), .L_S(LS), .B_H(displaymux_1_b_h), .B_M(displaymux_1_b_m), .B_S(displaymux_1_b_s), .AM(AM));
  not not_1 (BH, displaymux_1_b_h);
  _7_Segment_Display u_7_segment_display_2 (
    .g(controlled_buffer_2_out[6]), .f(controlled_buffer_2_out[5]), .a(controlled_buffer_2_out[4]),
    .b(controlled_buffer_2_out[3]), .e(controlled_buffer_2_out[0]), .d(controlled_buffer_2_out[1]),
    .c(controlled_buffer_2_out[2]));  // open: dp
  assign controlled_buffer_2_out = and_1_out ? indicatorconvector_2_output : 7'bz;  // Controlled_Buffer controlled_buffer_2
  IndicatorConvector indicatorconvector_2 (.\input (splitterhours_1_unit), .\output (indicatorconvector_2_output));
  LED led_1 (.in(displaymux_1_b_h));
  LED led_2 (.in(displaymux_1_b_m));
  LED led_3 (.in(displaymux_1_b_s));
  not not_2 (BM, displaymux_1_b_m);
  not not_3 (BS, displaymux_1_b_s);
  assign controlled_buffer_3_out = and_2_out ? indicatorconvector_3_output : 7'bz;  // Controlled_Buffer controlled_buffer_3
  IndicatorConvector indicatorconvector_3 (.\input (splittertime_1_out_2), .\output (indicatorconvector_3_output));
  _7_Segment_Display u_7_segment_display_3 (
    .g(controlled_buffer_3_out[6]), .f(controlled_buffer_3_out[5]), .a(controlled_buffer_3_out[4]),
    .b(controlled_buffer_3_out[3]), .e(controlled_buffer_3_out[0]), .d(controlled_buffer_3_out[1]),
    .c(controlled_buffer_3_out[2]));  // open: dp
  _7_Segment_Display u_7_segment_display_4 (
    .g(controlled_buffer_4_out[6]), .f(controlled_buffer_4_out[5]), .a(controlled_buffer_4_out[4]),
    .b(controlled_buffer_4_out[3]), .e(controlled_buffer_4_out[0]), .d(controlled_buffer_4_out[1]),
    .c(controlled_buffer_4_out[2]));  // open: dp
  and and_2 (and_2_out, L1, or_2_out, LM);
  or or_2 (or_2_out, clock_2_out, BM);
  Clock #(.highDuration(2)) clock_2 (.out(clock_2_out));
  State state_1 (
    .x1(buttonconv_1_x1), .x2(buttonconv_1_x2), .impuls(buttonconv_1_impuls), .R(R), .i1(i1), .i2(i2),
    .i3(i3), .i4(i4), .i5(i5), .i6(i6), .L1(L1), .L2(L2), .L3(L3), .L4(L4), .L5(L5), .L6(L6), .L7(L7),
    .L8(L8), .St(Stat));
  assign controlled_buffer_4_out = and_2_out ? indicatorconvector_4_output : 7'bz;  // Controlled_Buffer controlled_buffer_4
  IndicatorConvector indicatorconvector_4 (.\input (splittertime_1_out_3), .\output (indicatorconvector_4_output));
  SplitterTime splittertime_1 (.in_1(displaymux_1_d_m), .out_2(splittertime_1_out_2), .out_3(splittertime_1_out_3));
  _7_Segment_Display u_7_segment_display_5 (
    .g(controlled_buffer_5_out[6]), .f(controlled_buffer_5_out[5]), .a(controlled_buffer_5_out[4]),
    .b(controlled_buffer_5_out[3]), .e(controlled_buffer_5_out[0]), .d(controlled_buffer_5_out[1]),
    .c(controlled_buffer_5_out[2]));  // open: dp
  assign controlled_buffer_5_out = and_3_out ? indicatorconvector_5_output : 7'bz;  // Controlled_Buffer controlled_buffer_5
  IndicatorConvector indicatorconvector_5 (.\input (splittertime_2_out_2), .\output (indicatorconvector_5_output));
  SplitterTime splittertime_2 (.in_1(displaymux_1_d_s), .out_2(splittertime_2_out_2), .out_3(splittertime_2_out_3));
  _7_Segment_Display u_7_segment_display_6 (
    .g(controlled_buffer_6_out[6]), .f(controlled_buffer_6_out[5]), .a(controlled_buffer_6_out[4]),
    .b(controlled_buffer_6_out[3]), .e(controlled_buffer_6_out[0]), .d(controlled_buffer_6_out[1]),
    .c(controlled_buffer_6_out[2]));  // open: dp
  assign controlled_buffer_6_out = and_3_out ? indicatorconvector_6_output : 7'bz;  // Controlled_Buffer controlled_buffer_6
  and and_3 (and_3_out, L1, or_3_out, LS);
  or or_3 (or_3_out, clock_3_out, BS);
  Clock #(.highDuration(2)) clock_3 (.out(clock_3_out));
  IndicatorConvector indicatorconvector_6 (.\input (splittertime_2_out_3), .\output (indicatorconvector_6_output));
  Decoder_i1 decoder_i1_1 (
    .i1(i1), .q1(Stat[3]), .q2(Stat[2]), .q3(Stat[1]), .q4(Stat[0]), .INC_HOUR(decoder_i1_1_inc_hour),
    .INC_MIN(decoder_i1_1_inc_min), .INC_SEC(decoder_i1_1_inc_sec), .INC_TZ(TZ), .INC_ALARM_H(i_H),
    .INC_ALARM_M(i_M));
  TimeZone timezone_1 (.AM_PM(AM_PM), .Hours(Hours), .Inc(TZ), .Clk(Clk), .out_5(AM_PM_TZ), .out_6(Hours_TZ));
  LED led_4 (.in(sound_1_match));
  Sound sound_1 (.M(Minutes), .S(Seconds), .Match(sound_1_match));
  StopWatch stopwatch_1 (.Run(L3), .RESET_TIME(i4), .State(Stat), .CLK_1Hz(Clk), .SW_SEC(SW_SEC), .SW_MIN(SW_MIN));
  ALARM alarm_1 (
    .R(R), .i_M(i_M), .i_H(i_H), .A_P(AM_PM), .H(Hours), .M(Minutes), .S(Seconds), .Tgle(i5), .Cmd_stop(i6),
    .Clk(Clk), .A_M(A_M), .A_H(A_H), .AM_PM(AM_PM_AL), .ACTIVE(alarm_1_active), .ALR(alarm_1_alr));
  LED led_5 (.in(alarm_1_active));
  LED led_6 (.in(alarm_1_alr));
  ClockCore clockcore_1 (
    .RESET_TIME(R), .CLK_1Hz(Clk), .INC_HOUR(decoder_i1_1_inc_hour), .INC_MIN(decoder_i1_1_inc_min),
    .INC_SEC(decoder_i1_1_inc_sec), .RUN(L2), .SECONDS(Seconds), .MINUTES(Minutes), .HOURS(Hours),
    .AM_PM(AM_PM));

  // Other names for the same wires on the sheet: S[3:0] = Stat
endmodule

module ClockCore (
  input  RESET_TIME,
  input  CLK_1Hz,
  input  INC_HOUR,
  input  INC_MIN,
  input  INC_SEC,
  input  RUN,
  output [5:0] SECONDS,
  output [5:0] MINUTES,
  output [3:0] HOURS,
  output AM_PM
);

  wire and_1_out, and_2_out, and_3_out, d_ff_1_q, d_ff_2_q, Hours_Counter_carry, Minutes_Counter_carry,
       or_1_out, or_2_out, or_3_out, or_4_out, or_5_out, or_6_out, Seconds_Counter_carry;

  Clock clock_1 ();  // open: out
  and and_1 (and_1_out, CLK_1Hz, RUN);
  or or_1 (or_1_out, and_1_out, INC_SEC);
  or or_2 (or_2_out, INC_SEC, RUN);
  Counter #(.max('h3b), .width(6)) Seconds_Counter (
    .clr(RESET_TIME), .count(or_2_out), .clk(or_1_out), .carry(Seconds_Counter_carry), .Q(SECONDS));  // open: load, up, D
  or or_3 (or_3_out, INC_MIN, RUN);
  D_Flip_Flop d_ff_1 (.D(Seconds_Counter_carry), .clk(or_1_out), .Q(d_ff_1_q), .reset(RESET_TIME));  // open: Qn, preset
  and and_2 (and_2_out, d_ff_1_q, RUN);
  or or_4 (or_4_out, and_2_out, INC_MIN);
  Counter #(.max('h3b), .width(6)) Minutes_Counter (
    .clr(RESET_TIME), .count(or_3_out), .clk(or_4_out), .carry(Minutes_Counter_carry), .Q(MINUTES));  // open: load, up, D
  or or_5 (or_5_out, INC_HOUR, RUN);
  D_Flip_Flop d_ff_2 (.D(Minutes_Counter_carry), .clk(or_1_out), .Q(d_ff_2_q), .reset(RESET_TIME));  // open: Qn, preset
  and and_3 (and_3_out, d_ff_1_q, d_ff_2_q, RUN);
  Counter #(.max('hb), .width(4)) Hours_Counter (
    .clr(RESET_TIME), .count(or_5_out), .clk(or_6_out), .carry(Hours_Counter_carry), .Q(HOURS));  // open: load, up, D
  or or_6 (or_6_out, and_3_out, INC_HOUR);
  D_Flip_Flop d_ff_3 (.D(Hours_Counter_carry), .clk(or_1_out), .reset(RESET_TIME));  // open: Q, Qn, preset
  T_Flip_Flop AM_PM_FlipFlop (
    .T(Hours_Counter_carry), .clk(or_6_out), .Q(AM_PM), .reset(RESET_TIME));  // open: Qn, preset
endmodule

module ButtonConv (
  input  S,
  input  M,
  input  MS,
  input  P,
  output X1,
  output X2,
  output impuls
);

  or or_1 (impuls, P, MS, M, S);
  or or_2 (X1, MS, P);
  or or_3 (X2, M, P);
endmodule

module IndicatorConvector (
  input  [3:0] \input ,
  output [6:0] \output 
);

  wire and_1_out, and_2_out, and_3_out, and_4_out, and_5_out, and_6_out, and_7_out, and_8_out, and_9_out,
       and_10_out, and_11_out, and_12_out, and_13_out, and_14_out, and_15_out, and_16_out, and_17_out,
       and_18_out, and_19_out, and_20_out, and_21_out, and_22_out, and_23_out, and_24_out, and_25_out,
       and_26_out;

  and and_1 (and_1_out, \input [3], ~\input [2], ~\input [1]);  // AND_Gate
  and and_2 (and_2_out, ~\input [3], \input [2], ~\input [1]);  // AND_Gate
  and and_3 (and_3_out, ~\input [3], \input [1], ~\input [0]);  // AND_Gate
  and and_4 (and_4_out, ~\input [3], ~\input [2], \input [1]);  // AND_Gate
  and and_5 (and_5_out, \input [3], ~\input [2], ~\input [1]);  // AND_Gate
  and and_6 (and_6_out, ~\input [3], \input [2], ~\input [0]);  // AND_Gate
  and and_7 (and_7_out, ~\input [3], \input [2], ~\input [1]);  // AND_Gate
  and and_8 (and_8_out, ~\input [2], ~\input [1], ~\input [0]);  // AND_Gate
  and and_9 (and_9_out, ~\input [3], \input [1]);  // AND_Gate
  and and_10 (and_10_out, ~\input [3], \input [2], \input [0]);  // AND_Gate
  and and_11 (and_11_out, ~\input [2], ~\input [1], ~\input [0]);  // AND_Gate
  and and_12 (and_12_out, \input [3], ~\input [2], ~\input [1]);  // AND_Gate
  and and_13 (and_13_out, ~\input [2], ~\input [1]);  // AND_Gate
  and and_14 (and_14_out, ~\input [3], \input [1], \input [0]);  // AND_Gate
  and and_15 (and_15_out, ~\input [3], ~\input [2]);  // AND_Gate
  and and_16 (and_16_out, ~\input [3], ~\input [1], ~\input [0]);  // AND_Gate
  and and_17 (and_17_out, ~\input [3], \input [2]);  // AND_Gate
  and and_18 (and_18_out, ~\input [3], \input [0]);  // AND_Gate
  and and_19 (and_19_out, ~\input [2], ~\input [1]);  // AND_Gate
  and and_20 (and_20_out, ~\input [3], \input [1], ~\input [0]);  // AND_Gate
  and and_21 (and_21_out, ~\input [3], ~\input [2], \input [1]);  // AND_Gate
  and and_22 (and_22_out, ~\input [2], ~\input [1], ~\input [0]);  // AND_Gate
  and and_23 (and_23_out, ~\input [3], \input [2], ~\input [1], \input [0]);  // AND_Gate
  and and_24 (and_24_out, \input [3], ~\input [2], ~\input [1]);  // AND_Gate
  and and_25 (and_25_out, ~\input [3], \input [1], ~\input [0]);  // AND_Gate
  and and_26 (and_26_out, ~\input [2], ~\input [1], ~\input [0]);  // AND_Gate
  or f0 (\output [6], and_1_out, and_2_out, and_3_out, and_4_out);
  or f1 (\output [5], and_5_out, and_6_out, and_7_out, and_8_out);
  or f2 (\output [4], and_9_out, and_10_out, and_11_out, and_12_out);
  or f3 (\output [3], and_13_out, and_14_out, and_15_out, and_16_out);
  or f4 (\output [2], and_17_out, and_18_out, and_19_out);
  or f5 (\output [1], and_20_out, and_21_out, and_22_out, and_23_out, and_24_out);
  or f6 (\output [0], and_25_out, and_26_out);
  _7_Segment_Display u_7_segment_display_1 (
    .g(\output [6]), .f(\output [5]), .a(\output [4]), .b(\output [3]), .e(\output [0]), .d(\output [1]),
    .c(\output [2]));  // open: dp

  // Notes on the sheet:
  //   x0
  //   x1
  //   x0
  //   x1
  //   x2
  //   x3
  //   x2
  //   x3
endmodule

module F (
  input  q1,
  input  q2,
  input  q3,
  input  q4,
  input  x1,
  input  x2,
  input  Im,
  output i1,
  output i2,
  output i3,
  output i4,
  output i5,
  output i6,
  output Q_1,
  output Q_2,
  output Q_3,
  output Q_4
);

  wire and_1_out, and_2_out, and_3_out, and_4_out, and_5_out, and_6_out, and_7_out, and_8_out, and_9_out,
       and_10_out, and_11_out, or_1_out, or_2_out, or_3_out;

  and and_1 (and_1_out, q1, ~q3, ~x1, ~x2);  // AND_Gate
  and and_2 (and_2_out, q1, ~q2, q4, ~x1, ~x2);  // AND_Gate
  and and_3 (and_3_out, ~q1, ~q2, q3, ~q4, ~x1, ~x2);  // AND_Gate
  and and_4 (and_4_out, q1, ~q2, q3, ~q4, ~x1, ~x2);  // AND_Gate
  and and_5 (and_5_out, ~q1, q2, ~q3, ~x1, ~x2);  // AND_Gate
  and and_6 (and_6_out, ~q1, q2, ~q4, ~x1, ~x2);  // AND_Gate
  and and_7 (and_7_out, ~q1, ~q2, q3, q4, ~x1, ~x2);  // AND_Gate
  and and_8 (and_8_out, ~q1, q2, ~q3, x1, ~x2);  // AND_Gate
  and and_9 (and_9_out, ~q1, q2, ~q4, x1, ~x2);  // AND_Gate
  and and_10 (and_10_out, ~q1, q2, q3, q4, x1, ~x2);  // AND_Gate
  and and_11 (and_11_out, q1, q2, q3, q4, x1, ~x2);  // AND_Gate
  fQ1 fq1_1 (.q1(q1), .q2(q2), .q3(q3), .q4(q4), .x1(x1), .x2(x2), .Q_1(Q_1));
  fQ2 fq2_1 (.q1(q1), .q2(q2), .q3(q3), .q4(q4), .x1(x1), .x2(x2), .Q_2(Q_2));
  fQ3 fq3_1 (.q1(q1), .q2(q2), .q3(q3), .q4(q4), .x1(x1), .x2(x2), .Q_3(Q_3));
  fQ4 fq4_1 (.q1(q1), .q2(q2), .q3(q3), .q4(q4), .x1(x1), .x2(x2), .Q_4(Q_4));
  or or_1 (or_1_out, and_1_out, and_2_out, and_3_out);
  and and_12 (i2, and_4_out, Im);
  or or_2 (or_2_out, and_5_out, and_6_out, and_7_out);
  or or_3 (or_3_out, and_8_out, and_9_out);
  and and_13 (i5, and_10_out, Im);
  and and_14 (i6, and_11_out, Im);
  and and_15 (i1, or_1_out, Im);
  and and_16 (i3, or_2_out, Im);
  and and_17 (i4, or_3_out, Im);
endmodule

module fQ1 (
  input  q1,
  input  q2,
  input  q3,
  input  q4,
  input  x1,
  input  x2,
  output Q_1
);

  wire and_1_out, and_2_out, and_3_out, and_4_out, and_5_out, and_6_out, and_7_out, and_8_out, and_9_out;

  and and_1 (and_1_out, q1, ~q2, ~x2);  // AND_Gate
  and and_2 (and_2_out, q1, ~q3, ~x2);  // AND_Gate
  and and_3 (and_3_out, q4, x1, x2);
  and and_4 (and_4_out, ~q3, x1, x2);  // AND_Gate
  and and_5 (and_5_out, ~q2, x1, x2);  // AND_Gate
  and and_6 (and_6_out, ~q1, x1, x2);  // AND_Gate
  and and_7 (and_7_out, ~q2, ~q3, ~q4, x1);  // AND_Gate
  and and_8 (and_8_out, q1, q2, q3, q4, ~x1);  // AND_Gate
  and and_9 (and_9_out, q2, q3, q4, ~x1, ~x2);  // AND_Gate
  or or_1 (Q_1, and_1_out, and_2_out, and_3_out, and_4_out, and_5_out, and_6_out, and_7_out, and_8_out, and_9_out);
endmodule

module fQ2 (
  input  q1,
  input  q2,
  input  q3,
  input  q4,
  input  x1,
  input  x2,
  output Q_2
);

  wire and_1_out, and_2_out, and_3_out, and_4_out, and_5_out, and_6_out, and_7_out, and_8_out, and_9_out,
       and_10_out;

  and and_1 (and_1_out, ~q1, q2, x1);  // AND_Gate
  and and_2 (and_2_out, q4, x1, x2);
  and and_3 (and_3_out, ~q2, x1, x2);  // AND_Gate
  and and_4 (and_4_out, q1, ~q2, ~q3, x2);  // AND_Gate
  and and_5 (and_5_out, q2, ~q3, ~q4, x1);  // AND_Gate
  and and_6 (and_6_out, q2, ~q3, ~x1, ~x2);  // AND_Gate
  and and_7 (and_7_out, ~q1, q2, ~q4, ~x2);  // AND_Gate
  and and_8 (and_8_out, q1, ~q2, q3, q4, x1);  // AND_Gate
  and and_9 (and_9_out, q1, q2, q3, q4, ~x1);  // AND_Gate
  and and_10 (and_10_out, ~q1, ~q2, q3, q4, ~x1);  // AND_Gate
  or or_1 (Q_2, and_1_out, and_2_out, and_3_out, and_4_out, and_5_out, and_6_out, and_7_out, and_8_out, and_9_out, and_10_out);
endmodule

module fQ3 (
  input  q1,
  input  q2,
  input  q3,
  input  q4,
  input  x1,
  input  x2,
  output Q_3
);

  wire and_1_out, and_2_out, and_3_out, and_4_out, and_5_out, and_6_out, and_7_out, and_8_out, and_9_out,
       and_10_out, and_11_out, and_12_out;

  and and_1 (and_1_out, ~q1, q3, x1);  // AND_Gate
  and and_2 (and_2_out, q4, x1, x2);
  and and_3 (and_3_out, ~q3, x1, x2);  // AND_Gate
  and and_4 (and_4_out, q1, ~q2, ~q3, x2);  // AND_Gate
  and and_5 (and_5_out, q2, ~q3, q4, x1);  // AND_Gate
  and and_6 (and_6_out, ~q2, q3, ~q4, x1);  // AND_Gate
  and and_7 (and_7_out, ~q2, q3, ~q4, ~x2);  // AND_Gate
  and and_8 (and_8_out, ~q1, ~q2, q4, x2);  // AND_Gate
  and and_9 (and_9_out, ~q1, ~q2, ~q4, x1);  // AND_Gate
  and and_10 (and_10_out, q1, q3, q4, ~x1, ~x2);  // AND_Gate
  and and_11 (and_11_out, q1, q2, q3, q4, ~x1);  // AND_Gate
  and and_12 (and_12_out, ~q1, ~q2, ~q3, q4, ~x1);  // AND_Gate
  or or_1 (Q_3, and_1_out, and_2_out, and_3_out, and_4_out, and_5_out, and_6_out, and_7_out, and_8_out, and_9_out, and_10_out, and_11_out, and_12_out);
endmodule

module fQ4 (
  input  q1,
  input  q2,
  input  q3,
  input  q4,
  input  x1,
  input  x2,
  output Q_4
);

  wire and_1_out, and_2_out, and_3_out, and_4_out, and_5_out, and_6_out, and_7_out, and_8_out, and_9_out;

  and and_1 (and_1_out, q1, q4, ~x1, ~x2);  // AND_Gate
  and and_2 (and_2_out, ~q2, ~q3, ~x1, x2);  // AND_Gate
  and and_3 (and_3_out, ~q1, ~q2, ~x1, x2);  // AND_Gate
  and and_4 (and_4_out, q1, ~q2, ~q4, x1, ~x2);  // AND_Gate
  and and_5 (and_5_out, q1, q2, q3, q4, ~x1);  // AND_Gate
  and and_6 (and_6_out, q1, ~q3, ~q4, x1, ~x2);  // AND_Gate
  and and_7 (and_7_out, ~q1, q3, q4, x1, ~x2);  // AND_Gate
  and and_8 (and_8_out, ~q1, ~q2, q4, x1, ~x2);  // AND_Gate
  and and_9 (and_9_out, ~q1, q2, ~q3, ~q4, ~x1, ~x2);  // AND_Gate
  or or_1 (Q_4, and_1_out, and_2_out, and_3_out, and_4_out, and_5_out, and_6_out, and_7_out, and_8_out, and_9_out);
endmodule

module memory (
  input  impuls,
  input  R,
  input  q1,
  input  q2,
  input  q3,
  input  q4,
  output Q_1,
  output Q_2,
  output Q_3,
  output Q_4
);

  wire not_1_out;

  not not_1 (not_1_out, impuls);
  D_Flip_Flop d_ff_1 (.D(q1), .clk(not_1_out), .Q(Q_1), .reset(R));  // open: Qn, preset
  D_Flip_Flop d_ff_2 (.D(q2), .clk(not_1_out), .Q(Q_2), .reset(R));  // open: Qn, preset
  D_Flip_Flop d_ff_3 (.D(q3), .clk(not_1_out), .Q(Q_3), .reset(R));  // open: Qn, preset
  D_Flip_Flop d_ff_4 (.D(q4), .clk(not_1_out), .Q(Q_4), .reset(R));  // open: Qn, preset
endmodule

module FL (
  input  q1,
  input  q2,
  input  q3,
  input  q4,
  output L1,
  output L2,
  output L3,
  output L4,
  output L5,
  output L6,
  output L7,
  output L8
);

  wire and_1_out, and_3_out, and_4_out, and_5_out, and_6_out, and_7_out, and_8_out, and_9_out, and_10_out,
       and_11_out, and_12_out, and_13_out;

  or or_1 (L1, ~q1, ~q2, ~q3, q4);  // OR_Gate
  and and_1 (and_1_out, q2, q3);
  and and_2 (L3, ~q1, q2, ~q3, ~q4);  // AND_Gate
  and and_3 (and_3_out, ~q1, q2);  // AND_Gate
  and and_4 (and_4_out, q1, ~q2, ~q3);  // AND_Gate
  and and_5 (and_5_out, ~q1, q3, q4);  // AND_Gate
  and and_6 (and_6_out, q1, ~q2, ~q3);  // AND_Gate
  and and_7 (and_7_out, ~q1, q2, q3, q4);  // AND_Gate
  and and_8 (and_8_out, ~q1, ~q2, q3, ~q4);  // AND_Gate
  and and_9 (and_9_out, ~q2, ~q3, q4);  // AND_Gate
  and and_10 (and_10_out, q1, ~q2, q3, q4);  // AND_Gate
  and and_11 (and_11_out, q1, ~q2, ~q3, ~q4);  // AND_Gate
  and and_12 (and_12_out, q1, ~q2, ~q3, q4);  // AND_Gate
  and and_13 (and_13_out, q1, q2, ~q3, ~q4);  // AND_Gate
  and and_14 (L8, q1, q2, ~q3, q4);  // AND_Gate
  or or_2 (L2, ~q1, and_1_out);  // OR_Gate
  or or_3 (L4, and_3_out, and_4_out, and_5_out);
  or or_4 (L5, and_6_out, and_7_out, and_8_out, and_9_out);
  or or_5 (L6, and_10_out, and_11_out);
  or or_6 (L7, and_12_out, and_13_out);
endmodule

module State (
  input  x1,
  input  x2,
  input  impuls,
  input  R,
  output i1,
  output i2,
  output i3,
  output i4,
  output i5,
  output i6,
  output L1,
  output L2,
  output L3,
  output L4,
  output L5,
  output L6,
  output L7,
  output L8,
  output [3:0] St
);

  wire f_1_q_1, f_1_q_2, f_1_q_3, f_1_q_4, not_1_out, not_2_out;

  not not_1 (not_1_out, not_2_out);
  not not_2 (not_2_out, impuls);
  F f_1 (
    .q1(St[3]), .q2(St[2]), .q3(St[1]), .q4(St[0]), .x1(x1), .x2(x2), .Im(not_1_out), .i1(i1), .i2(i2),
    .i3(i3), .i4(i4), .i5(i5), .i6(i6), .Q_1(f_1_q_1), .Q_2(f_1_q_2), .Q_3(f_1_q_3), .Q_4(f_1_q_4));
  memory memory_1 (
    .impuls(impuls), .R(R), .q1(f_1_q_1), .q2(f_1_q_2), .q3(f_1_q_3), .q4(f_1_q_4), .Q_1(St[3]), .Q_2(St[2]),
    .Q_3(St[1]), .Q_4(St[0]));
  FL fl_1 (
    .q1(St[3]), .q2(St[2]), .q3(St[1]), .q4(St[0]), .L1(L1), .L2(L2), .L3(L3), .L4(L4), .L5(L5), .L6(L6),
    .L7(L7), .L8(L8));
endmodule

module Decoder_i1 (
  input  i1,
  input  q1,
  input  q2,
  input  q3,
  input  q4,
  output INC_HOUR,
  output INC_MIN,
  output INC_SEC,
  output INC_TZ,
  output INC_ALARM_H,
  output INC_ALARM_M
);

  wire not_1_out, not_2_out, not_3_out, not_4_out;

  not not_1 (not_1_out, q1);
  not not_2 (not_2_out, q2);
  not not_3 (not_3_out, q3);
  not not_4 (not_4_out, q4);
  and and_1 (INC_HOUR, i1, q1, not_2_out, q3, q4);
  and and_2 (INC_MIN, i1, q1, q2, not_3_out, not_4_out);
  and and_3 (INC_SEC, i1, q1, q2, not_3_out, q4);
  and and_4 (INC_TZ, i1, not_1_out, not_2_out, q3, not_4_out);
  and and_5 (INC_ALARM_H, i1, q1, not_2_out, not_3_out, not_4_out);
  and and_6 (INC_ALARM_M, i1, q1, not_2_out, not_3_out, q4);
endmodule

module SplitterTime (
  input  [5:0] in_1,
  output [3:0] out_2,
  output [3:0] out_3
);

  ROM #(.addrWidth(6)) rom_1 (.addr(in_1), .data({out_2, out_3}));

  // Notes on the sheet:
  //   contents of rom_1 (hex, n*v repeats v):
  //   0 1 2 3 4 5 6 7 8 9 10 11 12 13 14 15 16 17 18 19 20 21 22 23 24 25 26 27 28 29 30 31 32 33 34 35 36
  //   37 38 39 40 41 42 43 44 45 46 47 48 49 50 51 52 53 54 55 56 57 58 59
endmodule

module DisplayMux (
  input  [3:0] State,
  input  [3:0] H,
  input  [3:0] TZ_H,
  input  L4,
  input  [3:0] A_H,
  input  L5,
  input  [5:0] M,
  input  [5:0] SW_M,
  input  [5:0] A_M,
  input  [5:0] S,
  input  [5:0] SW_SEC,
  input  L6,
  input  L7,
  input  L8,
  input  AM_PM,
  input  AM_PM_AL,
  input  AM_PM_TZ,
  output [3:0] D_H,
  output [5:0] D_M,
  output [5:0] D_S,
  output L_H,
  output L_M,
  output L_S,
  output B_H,
  output B_M,
  output B_S,
  output AM
);

  wire comparator_1_eq, comparator_2_eq, comparator_3_eq;
  wire [1:0] rom_1_data;

  ROM #(.addrWidth(4), .dataWidth(2)) rom_1 (.addr(State), .data(rom_1_data));
  Multiplexer #(.select(2), .width(4)) multiplexer_1 (
    .in0(H), .in1(TZ_H), .in2(4'b0000), .in3(A_H), .out(D_H), .sel({L4, L5}));
  Multiplexer #(.select(2), .width(6)) multiplexer_2 (
    .in0(M), .in1(M), .in2(SW_M), .in3(A_M), .out(D_M), .sel({L4, L5}));
  Multiplexer #(.select(2), .width(6)) multiplexer_3 (
    .in0(S), .in1(S), .in2(SW_SEC), .in3({6{1'b0}}), .out(D_S), .sel({L4, L5}));
  Comparator #(.width(4)) comparator_1 (.a(State), .b(4'b1011), .eq(comparator_1_eq));  // open: gt, lt
  Comparator #(.width(4)) comparator_2 (.a(State), .b(4'b1100), .eq(comparator_2_eq));  // open: gt, lt
  Comparator #(.width(4)) comparator_3 (.a(State), .b(4'b1101), .eq(comparator_3_eq));  // open: gt, lt
  or or_1 (B_H, comparator_1_eq, L6);
  or or_2 (B_M, comparator_2_eq, L7);
  or or_3 (B_S, comparator_3_eq, L8);
  Comparator #(.width(4)) comparator_4 (.a(State), .b(4'b1101));  // open: gt, eq, lt
  Multiplexer #(.select(2)) multiplexer_4 (
    .in0(1'b0), .in1(AM_PM), .in2(AM_PM_AL), .in3(AM_PM_TZ), .out(AM), .sel(rom_1_data));
  ROM #(.addrWidth(4), .dataWidth(3)) rom_2 (.addr(State), .data({L_H, L_M, L_S}));

  // Notes on the sheet:
  //   contents of rom_1 (hex, n*v repeats v):
  //   1 3 3 4*0 2 2 2 4*1 0 2
  //   contents of rom_2 (hex, n*v repeats v):
  //   7 7 4 4*3 6 6 6 4*7 0 6
endmodule

module SplitterHours (
  input  [3:0] Hours,
  output [3:0] Tens,
  output [3:0] Unit
);

  wire comparator_1_eq;
  wire [3:0] multiplexer_1_out;

  Comparator #(.width(4)) comparator_1 (.a(Hours), .b(4'b0000), .eq(comparator_1_eq));  // open: gt, lt
  Multiplexer #(.width(4)) multiplexer_1 (.in0(Hours), .in1(4'b1100), .out(multiplexer_1_out), .sel(comparator_1_eq));
  Divider #(.width(4)) divider_1 (.a(multiplexer_1_out), .b(4'b1010), .out(Tens), .rem(Unit));  // open: upper
endmodule

module TimeZone (
  input  AM_PM,
  input  [3:0] Hours,
  input  Inc,
  input  Clk,
  output out_5,
  output [3:0] out_6
);

  wire comparator_1_lt, comparator_2_gt, not_1_out;
  wire [4:0] adder_1_out, bit_extender_1_out, multiplexer_1_out, multiplexer_2_out, subtractor_1_out,
       subtractor_2_out, TZ_offset_q;

  Counter #(.max('h17), .width(5)) TZ_offset (
    .count(Inc), .clk(Inc), .Q(TZ_offset_q));  // open: clr, load, up, D, carry
  assign bit_extender_1_out = {{1{1'b0}}, Hours};  // Bit_Extender bit_extender_1
  Subtractor #(.width(5)) subtractor_1 (.a(TZ_offset_q), .b(5'b01100), .out(subtractor_1_out));  // open: bin, bout
  Comparator #(.mode("unsigned"), .width(5)) comparator_1 (
    .a(TZ_offset_q), .b(5'b01100), .lt(comparator_1_lt));  // open: gt, eq
  not not_1 (not_1_out, comparator_1_lt);
  Multiplexer #(.width(5)) multiplexer_1 (
    .in0(TZ_offset_q), .in1(subtractor_1_out), .out(multiplexer_1_out), .sel(not_1_out));
  Adder #(.width(5)) adder_1 (.a(bit_extender_1_out), .b(multiplexer_1_out), .out(adder_1_out));  // open: cin, cout
  Comparator #(.mode("unsigned"), .width(5)) comparator_2 (
    .a(adder_1_out), .b(5'b01011), .gt(comparator_2_gt));  // open: eq, lt
  Subtractor #(.width(5)) subtractor_2 (.a(adder_1_out), .b(5'b01100), .out(subtractor_2_out));  // open: bin, bout
  Multiplexer #(.width(5)) multiplexer_2 (
    .in0(adder_1_out), .in1(subtractor_2_out), .out(multiplexer_2_out), .sel(comparator_2_gt));
  ExactlyOne xor_1 (.out(out_5), .in0(AM_PM), .in1(not_1_out), .in2(comparator_2_gt));
  Bit_Extender #(.in_width(5), .out_width(4), .\type ("zero")) bit_extender_2 (.in(multiplexer_2_out), .out(out_6));
endmodule

module StopWatch (
  input  Run,
  input  RESET_TIME,
  input  [3:0] State,
  input  CLK_1Hz,
  output [5:0] SW_SEC,
  output [5:0] SW_MIN
);

  wire and_1_out, comparator_1_eq, comparator_2_eq, d_ff_1_q, or_1_out, s_r_ff_1_q, Seconds_Counter_carry;

  Comparator #(.mode("unsigned"), .width(4)) comparator_1 (
    .a(State), .b(4'b0110), .eq(comparator_1_eq));  // open: gt, lt
  Comparator #(.mode("unsigned"), .width(4)) comparator_2 (
    .a(State), .b(4'b0101), .eq(comparator_2_eq));  // open: gt, lt
  or or_1 (or_1_out, comparator_1_eq, comparator_2_eq);
  Clock clock_1 ();  // open: out
  S_R_Flip_Flop s_r_ff_1 (.clk(CLK_1Hz), .Q(s_r_ff_1_q), .reset(or_1_out), .preset(Run));  // open: S, R, Qn
  Counter #(.max('h3b), .width(6)) Seconds_Counter (
    .clr(RESET_TIME), .count(s_r_ff_1_q), .clk(CLK_1Hz), .carry(Seconds_Counter_carry), .Q(SW_SEC));  // open: load, up, D
  D_Flip_Flop d_ff_1 (.D(Seconds_Counter_carry), .clk(CLK_1Hz), .Q(d_ff_1_q), .reset(RESET_TIME));  // open: Qn, preset
  and and_1 (and_1_out, d_ff_1_q, s_r_ff_1_q);
  Counter #(.max('h3b), .width(6)) Minutes_Counter (
    .clr(RESET_TIME), .clk(and_1_out), .Q(SW_MIN));  // open: load, up, count, D, carry
endmodule

module ALARM (
  input  R,
  input  i_M,
  input  i_H,
  input  A_P,
  input  [3:0] H,
  input  [5:0] M,
  input  [5:0] S,
  input  Tgle,
  input  Cmd_stop,
  input  Clk,
  output [5:0] A_M,
  output [3:0] A_H,
  output AM_PM,
  output ACTIVE,
  output ALR
);

  wire and_1_out, comparator_1_eq, comparator_2_eq, comparator_3_eq, comparator_4_eq, comparator_5_eq,
       Hours_Counter_carry, not_1_out, or_1_out, s_r_ff_1_qn;
  wire [3:0] counter_1_q;

  Clock clock_1 ();  // open: out
  Counter #(.max('h3b), .width(6)) Minutes_Counter (
    .clr(R), .count(Clk), .clk(i_M), .Q(A_M));  // open: load, up, D, carry
  Comparator #(.mode("unsigned"), .width(6)) comparator_1 (.a(A_M), .b(M), .eq(comparator_1_eq));  // open: gt, lt
  Counter #(.max('hb), .width(4)) Hours_Counter (
    .clr(R), .count(Clk), .clk(i_H), .carry(Hours_Counter_carry), .Q(A_H));  // open: load, up, D
  T_Flip_Flop t_ff_1 (.T(1'b1), .clk(not_1_out), .Q(ALR), .reset(R));  // open: Qn, preset
  not not_1 (not_1_out, Tgle);
  Counter #(.max('hb), .width(4)) counter_1 (
    .clr(s_r_ff_1_qn), .count(ACTIVE), .clk(Clk), .Q(counter_1_q));  // open: load, up, D, carry
  Comparator #(.mode("unsigned"), .width(4)) comparator_2 (.a(A_H), .b(H), .eq(comparator_2_eq));  // open: gt, lt
  T_Flip_Flop AM_PM_FlipFlop (.T(Hours_Counter_carry), .clk(i_H), .Q(AM_PM), .reset(R));  // open: Qn, preset
  Comparator #(.mode("unsigned"), .width(1)) comparator_3 (.a(AM_PM), .b(A_P), .eq(comparator_3_eq));  // open: gt, lt
  Comparator #(.mode("unsigned"), .width(4)) comparator_4 (
    .a(counter_1_q), .b(4'b1011), .eq(comparator_4_eq));  // open: gt, lt
  Comparator #(.mode("unsigned"), .width(6)) comparator_5 (.a({6{1'b0}}), .b(S), .eq(comparator_5_eq));  // open: gt, lt
  and and_1 (and_1_out, comparator_3_eq, comparator_2_eq, comparator_5_eq, comparator_1_eq, ALR);
  or or_1 (or_1_out, Cmd_stop, comparator_4_eq);
  S_R_Flip_Flop s_r_ff_1 (.Q(ACTIVE), .reset(or_1_out), .Qn(s_r_ff_1_qn), .preset(and_1_out));  // open: S, R, clk
endmodule

module Sound (
  input  [5:0] M,
  input  [5:0] S,
  output Match
);

  wire comparator_1_eq, comparator_2_eq, comparator_3_eq, comparator_4_eq, comparator_5_eq, or_1_out;

  Comparator #(.mode("unsigned"), .width(6)) comparator_1 (.a(S), .b({6{1'b0}}), .eq(comparator_1_eq));  // open: gt, lt
  Comparator #(.mode("unsigned"), .width(6)) comparator_2 (.a(M), .b({6{1'b0}}), .eq(comparator_2_eq));  // open: gt, lt
  Comparator #(.mode("unsigned"), .width(6)) comparator_3 (.a(M), .b(6'b101101), .eq(comparator_3_eq));  // open: gt, lt
  Comparator #(.mode("unsigned"), .width(6)) comparator_4 (.a(M), .b(6'b011110), .eq(comparator_4_eq));  // open: gt, lt
  Comparator #(.mode("unsigned"), .width(6)) comparator_5 (.a(M), .b(6'b001111), .eq(comparator_5_eq));  // open: gt, lt
  or or_1 (or_1_out, comparator_2_eq, comparator_3_eq, comparator_4_eq, comparator_5_eq);
  and and_1 (Match, or_1_out, comparator_1_eq);
endmodule

module Gen (
  output CLk
);

  Counter #(.max('h3f), .width(6)) counter_1 (.clk(CLk));  // open: clr, load, up, count, D, carry, Q
  Clock clock_1 (.out(CLk));
endmodule
